# Fritzing sketch HallwayLights (saved by Fritzing 0.9.2b)
breadboards: 1

parts:
  Part1 = Arduino Uno (Rev3)
  LED1 = RGB LED (com. cathode, rgb) [package="5 mm [THT]"]
  LED2 = RGB LED (com. cathode, rgb) [package="5 mm [THT]"]
  LED3 = RGB LED (com. cathode, rgb) [package="5 mm [THT]"]

nets:
  N1: Part1.D10_PWM/SS, Part1.D11_PWM/MOSI, Part1.D12/MISO, LED1.red_anode, LED2.blue_anode, LED3.green_anode
  N2: Part1.GND, LED1.common_cathode, LED2.common_cathode, LED3.common_cathode
